# Fritzing sketch chattertale_new_amp (saved by Fritzing 0.9.0b)
breadboards: 1

parts:
  Part1 = Arduino Uno (Rev3)
  S6 = Pushbutton [package="[SMD]"]
  S7 = Pushbutton [package="[SMD]"]
  S8 = Pushbutton [package="[SMD]"]
  S9 = Pushbutton [package="[SMD]"]
  S10 = Pushbutton [package="[SMD]"]
  R9 = Resistor [tolerance=±5% resistance=1k package="1206 [SMD]"]
  R10 = Resistor [tolerance=±5% resistance=1k package="1206 [SMD]"]  # not connected
  R11 = Resistor [tolerance=±5% resistance=1k package="1206 [SMD]"]
  R12 = Resistor [tolerance=±5% resistance=1k package="1206 [SMD]"]
  R13 = Resistor [tolerance=±5% resistance=1k package="1206 [SMD]"]
  MIC3 = MAX4466 Electret Microphone Breakout Board  # not connected
  U7 = AUDIO-JACK2 [package=audio-jack]  # not connected
  U8 = POT [package=pot_alpha_rv16af-20]
  AMP1 = MAX98306_Stereo_Amplifier
  SP2 = SPEAKER [package=pcb_mount_speaker]

nets:
  N1: Part1.A0, U8.S
  N2: Part1.D9_PWM, S8.Pin_3, S8.Pin_4
  N3: Part1.D10_PWM/SS, S7.Pin_3, S7.Pin_4
  N4: Part1.D2, S10.Pin_3, S10.Pin_4
  N5: Part1.D5_PWM, S9.Pin_3, S9.Pin_4
  N6: Part1.RESET, S6.Pin_3, S6.Pin_4
  N7: Part1.5V, U8.A, AMP1.connector1
  N8: Part1.GND, R9.Pin_0, R11.Pin_0, R12.Pin_0, R13.Pin_0, U8.E, AMP1.connector2
  N9: S6.Pin_1, S6.Pin_2
  N10: S7.Pin_1, S7.Pin_2, R11.Pin_1
  N11: S8.Pin_1, S8.Pin_2, R12.Pin_1
  N12: S9.Pin_1, S9.Pin_2, R13.Pin_1
  N13: S10.Pin_1, S10.Pin_2, R9.Pin_1
  N14: AMP1.connector5, AMP1.connector6
  N15: AMP1.connector11, SP2.+
  N16: AMP1.connector12, SP2.-

notes:
  voltage stepper
  Mic Out to M+ on music maker
  3.5mm jack to MusicMaker

custom parts:
  MAX4466 Electret Microphone Breakout Board: MAX4466 Electrec Microphone Breakout Board
