# Fritzing sketch 18 (saved by Fritzing 0.9.0b)
breadboards: 2

parts:
  U1 = LM386 [package=dip08]
  R1 = Resistor [tolerance=±5% resistance=1.2k package="1206 [SMD]"]
  C1 = Capacitor [package=cap-pth-5mm]
  R2 = Resistor [tolerance=±5% resistance=10 package=THT]
  C2 = Ceramic Capacitor [capacitance=0.1µF package="100 mil [THT, multilayer]"]
  C4 = Electrolytic Capacitor [capacitance=250µF package="100 mil [THT, electrolytic]"]  # not connected
  U5 = AUDIO-JACK2 [package=audio-jack]
  U4 = POT [package=pot_alpha_rv16af-20]

nets:
  N1: U1.GAIN, R1.Pin_0, C1.2
  N2: U1.-IN, U1.V-, C2.1, U4.E
  N3: U1.+IN, U4.S
  N4: U1.OUT, R2.Pin_0
  N5: R1.Pin_1, C1.1
  N6: R2.Pin_1, C2.0
  N7: U5.RSH, U4.A
