# Fritzing sketch 29 (saved by Fritzing 0.9.0b)
breadboards: 2

parts:
  U1 = LM386 [package=dip08]
  R1 = Resistor [tolerance=±5% resistance=1.2k package="1206 [SMD]"]
  C1 = Capacitor [package=cap-pth-5mm]
  R2 = Resistor [tolerance=±5% resistance=10 package=THT]
  C2 = Ceramic Capacitor [capacitance=0.1µF package="100 mil [THT, multilayer]"]
  C4 = Electrolytic Capacitor [capacitance=250µF package="100 mil [THT, electrolytic]"]  # not connected
  SP1 = SPEAKER [package=pcb_mount_speaker]
  C5 = Capacitor [package=cap-pth-small2]
  U5 = AUDIO-JACK2 [package=audio-jack]
  S1 = Pushbutton [package="[SMD]"]
  S2 = Pushbutton [package="[SMD]"]
  S3 = Pushbutton [package="[SMD]"]
  S4 = Pushbutton [package="[SMD]"]
  S5 = Pushbutton [package="[SMD]"]
  R3 = Resistor [tolerance=±5% resistance=1k package="1206 [SMD]"]
  R4 = Resistor [tolerance=±5% resistance=1k package="1206 [SMD]"]  # not connected
  R5 = Resistor [tolerance=±5% resistance=1k package="1206 [SMD]"]
  R6 = Resistor [tolerance=±5% resistance=1k package="1206 [SMD]"]  # not connected
  R7 = Resistor [tolerance=±5% resistance=1k package="1206 [SMD]"]
  U6 = POT [package=pot_alpha_rv16af-20]  # not connected
  LED1 = LED - 5mm [color="Red (633nm)" package="5 mm [THT]"]
  R8 = Resistor [tolerance=±5% resistance=1k package="1206 [SMD]"]
  U4 = POT [package=pot_alpha_rv16af-20]

nets:
  N1: U1.GAIN, R1.Pin_0, C1.2
  N2: U1.-IN, U1.V-, C2.1, SP1.+, C5.2, U4.E
  N3: U1.+IN, U4.S
  N4: U1.OUT, R2.Pin_0
  N5: U1.BP, C5.1
  N6: R1.Pin_1, C1.1
  N7: R2.Pin_1, C2.0
  N8: U5.RSH, U4.A
  N9: S1.Pin_1, S1.Pin_2, R3.Pin_1
  N10: S1.Pin_3, S1.Pin_4
  N11: S2.Pin_1, S2.Pin_2
  N12: S2.Pin_3, S2.Pin_4
  N13: S3.Pin_1, S3.Pin_2, R5.Pin_1
  N14: S3.Pin_3, S3.Pin_4
  N15: S4.Pin_1, S4.Pin_2
  N16: S4.Pin_3, S4.Pin_4
  N17: S5.Pin_1, S5.Pin_2, R7.Pin_1
  N18: S5.Pin_3, S5.Pin_4
  N19: R3.Pin_0, R5.Pin_0, R7.Pin_0, LED1.cathode
  N20: LED1.anode, R8.Pin_1
