# Fritzing sketch 8 (saved by Fritzing 0.9.0b)
breadboards: 2

parts:
  U1 = LM386 [package=dip08]
  R1 = Resistor [tolerance=±5% resistance=1.2k package="1206 [SMD]"]
  C1 = Capacitor [package=cap-pth-5mm]

nets:
  N1: U1.GAIN, R1.Pin_0, C1.2
  N2: U1.-IN, U1.V-
  N3: R1.Pin_1, C1.1
